// Logisim project Project CSN 221.circ as structural Verilog: 14 circuits, main circuit main
module main (
  input  in_1,
  input  [3:0] in_2
);

  wire alu_1_equal_to, alu_1_greater_than, Clock, flags_1_flagse, flags_1_flagsgt, Hit_Miss, IMMEDIATE_BIT,
       IsBeq, IsBgt, IsBranchTaken, IsCall, IsImmediate, IsLd, IsRet, IsSt, IsUBranch, IsWb, or_1_out;
  wire [3:0] multiplexer_4_out, Reg1_Address, Reg2_Address;
  wire [12:0] ALUsignals;
  wire [31:0] aluResult, branchPC, data, Display_Data, Instruction, ldResult, OPERAND_1, OPERAND_2,
       OPERAND_2_prime, PC, pc_1;

  Clock clock_1 (.out(Clock));
  or or_1 (or_1_out, IsLd, IsSt);
  Program_Counter program_counter_1 (
    .Instruction(PC), .Hit_Miss(Hit_Miss), .Load_Store(or_1_out), .isBranchTaken(IsBranchTaken),
    .branchPC(branchPC), .Clock(Clock), .Reset(in_1));  // open: Input___Enable, Input_Data
  ALU alu_1 (
    .A(OPERAND_1), .B(OPERAND_2_prime), .Alusignals(ALUsignals), .EQUAL_TO(alu_1_equal_to),
    .aluResult(aluResult), .GREATER_THAN(alu_1_greater_than));
  Adder #(.width(32)) adder_1 (.a(PC), .b(32'h1), .out(pc_1));  // open: cin, cout
  Immediate_Calculation immediate_calculation_1 (
    .Operand_1(OPERAND_1), .isRet(IsRet), .isImmediate(IsImmediate), .Operand_2(OPERAND_2),
    .Instruction({Instruction[31:27], IMMEDIATE_BIT, Instruction[25:0]}), .PC(PC),
    .Operand_2_prime(OPERAND_2_prime), .branchTarget(branchPC));
  Cache_Management cache_management_1 (
    .Load(IsLd), .Store(IsSt), .Write_Data(OPERAND_2), .Output_Data(ldResult), .address(aluResult),
    .Clock(Clock), .out_6(Hit_Miss));
  RAM #(.addrWidth(24), .dataWidth(32)) ram_1 (
    .addr(PC[23:0]), .data({Instruction[31:27], IMMEDIATE_BIT, Instruction[25:0]}), .clk(Clock));  // open: sel, ld, clr
  Multiplexer #(.width(4), .enable("false")) multiplexer_1 (
    .in0(Instruction[17:14]), .in1(Instruction[25:22]), .out(Reg2_Address), .sel(IsSt));
  Multiplexer #(.width(4), .enable("false")) multiplexer_2 (
    .in0(Instruction[21:18]), .in1(4'b1111), .out(Reg1_Address), .sel(IsRet));
  Flags flags_1 (
    .GREATER_THAN(alu_1_greater_than), .isCmp(ALUsignals[0]), .EQUAL_TO(alu_1_equal_to),
    .flagsGT(flags_1_flagsgt), .flagsE(flags_1_flagse), .in_1(Clock));
  Branch branch_1 (
    .isBeq(IsBeq), .flagsE(flags_1_flagse), .isUBranch(IsUBranch), .isBranchTaken(IsBranchTaken),
    .isBgt(IsBgt), .flagsGT(flags_1_flagsgt));
  Control_Unit control_unit_1 (
    .opcode(Instruction[31:27]), .I_bit(IMMEDIATE_BIT), .isBgt(IsBgt), .isSt(IsSt), .isLd(IsLd),
    .isCall(IsCall), .isUbranch(IsUBranch), .isWb(IsWb), .ALUsignals(ALUsignals), .isImmediate(IsImmediate),
    .isBeq(IsBeq), .isRet(IsRet));
  Register_File register_file_1 (
    .Op1(OPERAND_1), .Op2(OPERAND_2), .isWb(IsWb), .Reg1_Address(Reg1_Address), .Reg2_Address(Reg2_Address),
    .data(data), .Display(Display_Data), .Display_reg_Address(Instruction[25:22]),
    .Write_Address(multiplexer_4_out), .Clock(Clock), .Reset(in_1));
  Multiplexer #(.select(2), .width(32)) multiplexer_3 (
    .in0(aluResult), .in1(ldResult), .in2(pc_1), .out(data), .sel({IsCall, IsLd}));  // open: in3, en
  Hex_Digit_Display hex_digit_display_1 (.value(Instruction[25:22]));  // open: dp
  Hex_Digit_Display hex_digit_display_2 (.value(Display_Data[31:28]));  // open: dp
  Hex_Digit_Display hex_digit_display_3 (.value(Display_Data[27:24]));  // open: dp
  Hex_Digit_Display hex_digit_display_4 (.value(Display_Data[23:20]));  // open: dp
  Hex_Digit_Display hex_digit_display_5 (.value(Display_Data[19:16]));  // open: dp
  Hex_Digit_Display hex_digit_display_6 (.value(Display_Data[15:12]));  // open: dp
  Hex_Digit_Display hex_digit_display_7 (.value(Display_Data[7:4]));  // open: dp
  Hex_Digit_Display hex_digit_display_8 (.value(Display_Data[11:8]));  // open: dp
  Hex_Digit_Display hex_digit_display_9 (.value(Display_Data[3:0]));  // open: dp
  Multiplexer #(.width(4), .enable("false")) multiplexer_4 (
    .in0(Instruction[25:22]), .in1(4'b1111), .out(multiplexer_4_out), .sel(IsCall));

  // Other names for the same wires on the sheet: rd[3:0] = Instruction[25:22]; Instruction[26] = IMMEDIATE_BIT;
  //   OPCODE[4:0] = Instruction[31:27]; Reset = in_1

  // Notes on the sheet:
  //   For Reseting
  //   Clock
  //   Memory Address Register
  //   Clock
  //   ARITHMETIC LOGIC UNIT
  //   For Loading data from memory
  //   For calculating the next effective default address
  //   Data loaded from memory
  //   For Storing data into memory
  //   Memory Data Register
  //   Destination Register
  //   Destination Register Value
endmodule

// Memory with Cache Management
module Cache_Management (
  input  Clock,
  input  [31:0] address,
  input  Load,
  input  Store,
  input  [31:0] Write_Data,
  output out_6,
  output [31:0] Output_Data
);

  wire and_1_out, and_2_out, and_3_out, and_5_out, evict, eviction_done, Load_Store, loading_done,
       Modified_Bit, not_1_out, not_2_out, not_3_out, not_4_out, not_5_out, or_1_out, or_2_out, or_3_out,
       or_4_out, or_5_out, or_6_out;
  wire [9:0] Index;
  wire [12:0] data_array_address, eviction_block_adderss, Index_Offset, multiplexer_1_out, multiplexer_2_out,
       tag;
  wire [23:0] memory_address, memory_address_t, memory_address_to_load_to_cache, multiplexer_4_out;
  wire [31:0] Dara_Array_data, data_from_main_memory, multiplexer_3_out;

  Tag_Array tag_array_1 (
    .index_offset(Index_Offset), .Hit_Miss(out_6), .Index(Index), .Loading_Done(loading_done), .Tag(tag),
    .Modified_Bit(Modified_Bit), .Eviction_Done(eviction_done), .Load(Load), .Store(Store),
    .Address(address), .Clock(Clock));  // open: valid
  Eviction eviction_1 (
    .Hit_Miss(out_6), .Modified_Bit(Modified_Bit), .Block_Address(eviction_block_adderss),
    .Memory_Address(memory_address), .Index(Index), .Tag(tag), .Eviction_Done(eviction_done), .Clock(Clock),
    .Load_Store(Load_Store));
  Loading loading_1 (
    .Hit_Miss(out_6), .Modified_Bit(Modified_Bit), .Address(address),
    .Memory_Address(memory_address_to_load_to_cache), .Data_Array_Address(data_array_address), .Clock(Clock),
    .Loading_Done(loading_done), .Load_Store(Load_Store));
  and and_1 (and_1_out, out_6, Store);
  Multiplexer #(.width(13)) multiplexer_1 (
    .in0(data_array_address), .in1(eviction_block_adderss), .out(multiplexer_1_out), .sel(Modified_Bit));  // open: en
  Multiplexer #(.width(13)) multiplexer_2 (
    .in0(multiplexer_1_out), .in1(Index_Offset), .out(multiplexer_2_out), .sel(out_6));  // open: en
  Multiplexer #(.width(32)) multiplexer_3 (
    .in0(data_from_main_memory), .in1(Write_Data), .out(multiplexer_3_out), .sel(out_6));  // open: en
  or or_1 (or_1_out, and_1_out, and_2_out);
  and and_2 (and_2_out, not_1_out, or_2_out, not_2_out);
  not not_1 (not_1_out, out_6);
  or or_2 (or_2_out, Load, Store);
  Data_Array Dara_Array (
    .Data_Address(multiplexer_2_out), .Data(Dara_Array_data), .Data_to_be_written(multiplexer_3_out),
    .Clock(Clock), .store(or_1_out), .load(or_3_out));
  not not_2 (not_2_out, Modified_Bit);
  or or_3 (or_3_out, evict, and_3_out);
  and and_3 (and_3_out, out_6, Load);
  or or_4 (or_4_out, Load, Store);
  and and_4 (evict, or_4_out, not_3_out, Modified_Bit);
  not not_3 (not_3_out, out_6);
  or or_5 (or_5_out, out_6, Modified_Bit);
  and and_5 (and_5_out, or_6_out, not_4_out, not_5_out);
  or or_6 (or_6_out, Load, Store);
  not not_4 (not_4_out, out_6);
  Multiplexer #(.width(24)) multiplexer_4 (
    .in0(memory_address_to_load_to_cache), .in1(memory_address_t), .out(multiplexer_4_out), .sel(or_5_out));  // open: en
  Memory memory_1 (
    .Memory_Address_Register(multiplexer_4_out), .out_7(data_from_main_memory),
    .Memory_Buffer_Register(Dara_Array_data), .Clock(Clock), .Store(evict), .Load(and_5_out));  // open: Reset
  not not_5 (not_5_out, Modified_Bit);
  assign Output_Data = out_6 ? Dara_Array_data : 32'bz;  // Controlled_Buffer controlled_buffer_1
  or or_7 (Load_Store, Load, Store);

  // Other names for the same wires on the sheet: Hit_Miss = out_6
endmodule

module Tag_Array (
  input  Clock,
  input  [31:0] Address,
  input  Loading_Done,
  input  Eviction_Done,
  input  Store,
  input  Load,
  output [12:0] index_offset,
  output [9:0] Index,
  output Hit_Miss,
  output Modified_Bit,
  output valid,
  output [12:0] Tag
);

  wire and_1_out, comparator_1_eq, or_1_out;
  wire [12:0] multiplexer_1_out;

  Multiplexer #(.select(2), .width(13)) multiplexer_1 (
    .in0({2'b11, Tag[10:0]}), .in1({2'b10, Tag[10:0]}), .in2({2'b10, Address[23:13]}),
    .out(multiplexer_1_out), .sel({Loading_Done, Eviction_Done}));  // open: in3, en
  or or_1 (or_1_out, Loading_Done, Eviction_Done, and_1_out);
  and and_1 (and_1_out, Store, Hit_Miss);
  RAM #(.addrWidth(10), .dataWidth(13), .bus("separate")) ram_1 (
    .addr(Address[12:3]), .din(multiplexer_1_out), .data({Tag[12], Modified_Bit, Tag[10:0]}), .str(or_1_out),
    .clk(Clock), .ld(1'b1));  // open: sel, clr
  Comparator #(.width(11)) comparator_1 (.a(Address[23:13]), .b(Tag[10:0]), .eq(comparator_1_eq));  // open: gt, lt
  and and_2 (Hit_Miss, comparator_1_eq, Tag[12]);

  assign Index = Address[12:3];
  assign index_offset = Address[12:0];
  assign Tag[11] = Modified_Bit;
  assign valid = Tag[12];

  // Other names for the same wires on the sheet: block_address[10:0] = Address[23:13];
  //   select[1:0] = {Loading_Done, Eviction_Done}; loaded_address[10:0] = Tag[10:0]
endmodule

module Data_Array (
  input  [12:0] Data_Address,
  input  Clock,
  input  [31:0] Data_to_be_written,
  input  load,
  input  store,
  output [31:0] Data
);

  RAM #(.addrWidth(13), .dataWidth(32), .bus("separate")) ram_1 (
    .addr(Data_Address), .din(Data_to_be_written), .data(Data), .str(store), .clk(Clock), .ld(load));  // open: sel, clr
endmodule

// Main Memory
module Memory (
  input  [23:0] Memory_Address_Register,
  input  Clock,
  input  [31:0] Memory_Buffer_Register,
  input  Reset,
  input  Store,
  input  Load,
  output [31:0] out_7
);

  RAM #(.addrWidth(24), .dataWidth(32), .bus("separate")) ram_1 (
    .addr(Memory_Address_Register), .din(Memory_Buffer_Register), .data(out_7), .str(Store), .clk(Clock),
    .ld(Load), .clr(Reset));  // open: sel
endmodule

module Eviction (
  input  Hit_Miss,
  input  Load_Store,
  input  Modified_Bit,
  input  Clock,
  input  [9:0] Index,
  input  [12:0] Tag,
  output [12:0] Block_Address,
  output [23:0] Memory_Address,
  output Eviction_Done
);

  wire and_1_out, not_1_out;

  not not_1 (not_1_out, Hit_Miss);
  and and_1 (and_1_out, not_1_out, Load_Store, Modified_Bit);
  Counter #(.width(3), .max('h7)) counter_1 (
    .count(and_1_out), .Q(Block_Address[2:0]), .carry(Eviction_Done), .clk(Clock));  // open: load, D, clr

  assign Block_Address[12:3] = Index;
  assign Memory_Address = {Tag[10:0], Index, Block_Address[2:0]};
endmodule

module Loading (
  input  Hit_Miss,
  input  Load_Store,
  input  Modified_Bit,
  input  Clock,
  input  [31:0] Address,
  output [23:0] Memory_Address,
  output Loading_Done,
  output [12:0] Data_Array_Address
);

  wire and_1_out, not_1_out, not_2_out;

  not not_1 (not_1_out, Hit_Miss);
  not not_2 (not_2_out, Modified_Bit);
  and and_1 (and_1_out, not_1_out, Load_Store, not_2_out);
  Counter #(.width(3), .max('h7)) counter_1 (
    .count(and_1_out), .Q(Data_Array_Address[2:0]), .carry(Loading_Done), .clk(Clock));  // open: load, D, clr

  assign Data_Array_Address[12:3] = Address[12:3];
  assign Memory_Address = {Address[23:3], Data_Array_Address[2:0]};
endmodule

module ALU (
  input  [31:0] A,
  input  [31:0] B,
  input  [12:0] Alusignals,
  output [31:0] aluResult,
  output GREATER_THAN,
  output EQUAL_TO
);

  wire [31:0] ADDITION, AND, AND_t, ARITHMETIC_RIGHT_SHIFT, DIVISION, LEFT_SHIFT, MULTIPLICATION, NOT, OR,
       REMAINDER, RIGHT_SHIFT, SUBTRACTION;

  Adder #(.width(32)) adder_1 (.a(A), .b(B), .out(ADDITION));  // open: cin, cout
  Multiplier #(.width(32)) multiplier_1 (.a(A), .b(B), .out(MULTIPLICATION));  // open: cin, cout
  Comparator #(.width(32)) comparator_1 (.a(A), .b(B), .gt(GREATER_THAN), .eq(EQUAL_TO));  // open: lt
  Shifter #(.width(32), .shift("lr")) shifter_1 (.in(A), .\dist (B[4:0]), .out(RIGHT_SHIFT));
  assign NOT = ~A;  // NOT_Gate not_1, 32 bits wide
  assign OR = A | B;  // OR_Gate or_1, 32 bits wide
  Subtractor #(.width(32)) subtractor_1 (.a(A), .b(B), .out(SUBTRACTION));  // open: bin, bout
  Divider #(.width(32)) divider_1 (.a(A), .b(B), .out(DIVISION), .rem(REMAINDER));  // open: upper
  Shifter #(.width(32)) shifter_2 (.in(A), .\dist (B[4:0]), .out(LEFT_SHIFT));
  Shifter #(.width(32), .shift("ar")) shifter_3 (.in(A), .\dist (B[4:0]), .out(ARITHMETIC_RIGHT_SHIFT));
  assign AND_t = A & B;  // AND_Gate and_1, 32 bits wide
  assign aluResult = Alusignals[1] ? ADDITION : 32'bz;  // Controlled_Buffer controlled_buffer_1
  assign aluResult = Alusignals[2] ? SUBTRACTION : 32'bz;  // Controlled_Buffer controlled_buffer_2
  assign aluResult = Alusignals[3] ? MULTIPLICATION : 32'bz;  // Controlled_Buffer controlled_buffer_3
  assign aluResult = Alusignals[4] ? DIVISION : 32'bz;  // Controlled_Buffer controlled_buffer_4
  assign aluResult = Alusignals[5] ? REMAINDER : 32'bz;  // Controlled_Buffer controlled_buffer_5
  assign aluResult = Alusignals[6] ? B : 32'bz;  // Controlled_Buffer controlled_buffer_6
  assign aluResult = Alusignals[7] ? LEFT_SHIFT : 32'bz;  // Controlled_Buffer controlled_buffer_7
  assign aluResult = Alusignals[8] ? RIGHT_SHIFT : 32'bz;  // Controlled_Buffer controlled_buffer_8
  assign aluResult = Alusignals[9] ? ARITHMETIC_RIGHT_SHIFT : 32'bz;  // Controlled_Buffer controlled_buffer_9
  assign aluResult = Alusignals[10] ? NOT : 32'bz;  // Controlled_Buffer controlled_buffer_10
  assign aluResult = Alusignals[11] ? AND : 32'bz;  // Controlled_Buffer controlled_buffer_11
  assign aluResult = Alusignals[12] ? OR : 32'bz;  // Controlled_Buffer controlled_buffer_12

  // Notes on the sheet:
  //   OPERAND 1
  //   ADDER : ADDITION
  //   SHIFTER : LSR
  //   NOT GATE
  //   OR GATE
  //   MULTIPLICATOR : MULTIPLICATION
  //   COMPARATOR :  COMPARE
  //   OPERAND 2
  //   DIVIDER :  DIVISION
  //   SHIFTER : LSL
  //   SHIFTER : ASR
  //   AND GATE
  //   SUBTRACTOR :  SUBTRACTION
  //   RESULT
  //   ALU SIGNALS
endmodule

module Register_File (
  input  Reset,
  input  Clock,
  input  [31:0] data,
  input  isWb,
  input  [3:0] Reg1_Address,
  input  [3:0] Write_Address,
  input  [3:0] Reg2_Address,
  input  [3:0] Display_reg_Address,
  output [31:0] Op1,
  output [31:0] Op2,
  output [31:0] Display
);

  wire counter_1_q, isWb0, isWb1, isWb2, isWb3, isWb4, isWb5, isWb6, isWb7, isWb8, isWb9, isWb10, isWb11,
       isWb12, isWb13, isWb14, isWb15, not_1_out, or_1_out;
  wire [31:0] multiplexer_1_out, read_r0, read_r1, read_r2, read_r3, read_r4, read_r5, read_r6, read_r7,
       read_r8, read_r9, read_r10, read_r11, read_r12, read_r13, read_r14, read_r15;

  Demultiplexer #(.select(4)) demultiplexer_1 (
    .out0(isWb0), .out1(isWb1), .out2(isWb2), .out3(isWb3), .out4(isWb4), .out5(isWb5), .out6(isWb6),
    .out7(isWb7), .out8(isWb8), .out9(isWb9), .out10(isWb10), .out11(isWb11), .out12(isWb12), .out13(isWb13),
    .out14(isWb14), .out15(isWb15), .in(isWb), .sel(Write_Address));  // open: en
  Multiplexer #(.width(32), .enable("false")) multiplexer_1 (
    .in0(32'hffffff), .in1(data), .out(multiplexer_1_out), .sel(counter_1_q));
  Counter #(.width(1), .max('h1), .ongoal("stay")) counter_1 (
    .Q(counter_1_q), .clk(Clock), .clr(Reset));  // open: load, D, count, carry
  not not_1 (not_1_out, counter_1_q);
  or or_1 (or_1_out, isWb14, not_1_out);
  Register #(.width(32)) r0 (.D(data), .en(isWb0), .Q(read_r0), .clk(Clock), .clr(Reset));
  Register #(.width(32)) r1 (.D(data), .en(isWb1), .Q(read_r1), .clk(Clock), .clr(Reset));
  Register #(.width(32)) r2 (.D(data), .en(isWb2), .Q(read_r2), .clk(Clock), .clr(Reset));
  Register #(.width(32)) r3 (.D(data), .en(isWb3), .Q(read_r3), .clk(Clock), .clr(Reset));
  Register #(.width(32)) r4 (.D(data), .en(isWb4), .Q(read_r4), .clk(Clock), .clr(Reset));
  Register #(.width(32)) r5 (.D(data), .en(isWb5), .Q(read_r5), .clk(Clock), .clr(Reset));
  Register #(.width(32)) r6 (.D(data), .en(isWb6), .Q(read_r6), .clk(Clock), .clr(Reset));
  Register #(.width(32)) r7 (.D(data), .en(isWb7), .Q(read_r7), .clk(Clock), .clr(Reset));
  Register #(.width(32)) r8 (.D(data), .en(isWb8), .Q(read_r8), .clk(Clock), .clr(Reset));
  Register #(.width(32)) r9 (.D(data), .en(isWb9), .Q(read_r9), .clk(Clock), .clr(Reset));
  Register #(.width(32)) r10 (.D(data), .en(isWb10), .Q(read_r10), .clk(Clock), .clr(Reset));
  Register #(.width(32)) r11 (.D(data), .en(isWb11), .Q(read_r11), .clk(Clock), .clr(Reset));
  Register #(.width(32)) r12 (.D(data), .en(isWb12), .Q(read_r12), .clk(Clock), .clr(Reset));
  Register #(.width(32)) r13 (.D(data), .en(isWb13), .Q(read_r13), .clk(Clock), .clr(Reset));
  Register #(.width(32)) r14 (.D(multiplexer_1_out), .en(or_1_out), .Q(read_r14), .clk(Clock), .clr(Reset));
  Register #(.width(32)) r15 (.D(data), .en(isWb15), .Q(read_r15), .clk(Clock), .clr(Reset));
  Multiplexer #(.select(4), .width(32)) multiplexer_2 (
    .in0(read_r0), .in1(read_r1), .in2(read_r2), .in3(read_r3), .in4(read_r4), .in5(read_r5), .in6(read_r6),
    .in7(read_r7), .in8(read_r8), .in9(read_r9), .in10(read_r10), .in11(read_r11), .in12(read_r12),
    .in13(read_r13), .in14(read_r14), .in15(read_r15), .out(Op1), .sel(Reg1_Address));  // open: en
  Multiplexer #(.select(4), .width(32)) multiplexer_3 (
    .in0(read_r0), .in1(read_r1), .in2(read_r2), .in3(read_r3), .in4(read_r4), .in5(read_r5), .in6(read_r6),
    .in7(read_r7), .in8(read_r8), .in9(read_r9), .in10(read_r10), .in11(read_r11), .in12(read_r12),
    .in13(read_r13), .in14(read_r14), .in15(read_r15), .out(Display), .sel(Display_reg_Address));  // open: en
  Multiplexer #(.select(4), .width(32)) multiplexer_4 (
    .in0(read_r0), .in1(read_r1), .in2(read_r2), .in3(read_r3), .in4(read_r4), .in5(read_r5), .in6(read_r6),
    .in7(read_r7), .in8(read_r8), .in9(read_r9), .in10(read_r10), .in11(read_r11), .in12(read_r12),
    .in13(read_r13), .in14(read_r14), .in15(read_r15), .out(Op2), .sel(Reg2_Address));  // open: en

  // Other names for the same wires on the sheet: clk = Clock; WbData[31:0] = data
endmodule

// CONTROL UNIT
module Control_Unit (
  input  [4:0] opcode,
  input  I_bit,
  output isBgt,
  output isSt,
  output isLd,
  output isCall,
  output isUbranch,
  output isWb,
  output [12:0] ALUsignals,
  output isImmediate,
  output isBeq,
  output isRet
);

  wire and_1_out, and_2_out, and_3_out, and_4_out, and_5_out, and_10_out, and_11_out, nand_1_out;

  nand nand_1 (nand_1_out, opcode[0], opcode[1]);
  and isNot (ALUsignals[10], ~opcode[0], ~opcode[1], ~opcode[2], opcode[3], ~opcode[4]);  // AND_Gate
  and and_1 (and_1_out, opcode[0], ~opcode[1], opcode[2], ~opcode[4]);  // AND_Gate
  and and_2 (and_2_out, opcode[0], opcode[2], opcode[3], ~opcode[4]);  // AND_Gate
  and and_3 (and_3_out, opcode[4], nand_1_out);
  and and_4 (and_4_out, ~opcode[0], ~opcode[1], ~opcode[2], ~opcode[3], ~opcode[4]);  // AND_Gate
  and and_5 (and_5_out, opcode[1], opcode[2], opcode[3], ~opcode[4]);  // AND_Gate
  and isAnd (ALUsignals[11], ~opcode[0], opcode[1], opcode[2], ~opcode[3], ~opcode[4]);  // AND_Gate
  and and_6 (isBgt, opcode[0], ~opcode[1], ~opcode[2], ~opcode[3], opcode[4]);  // AND_Gate
  nor nor_1 (isWb, and_1_out, and_2_out, and_3_out);
  or isAdd (ALUsignals[1], and_4_out, and_5_out);
  and isSub (ALUsignals[2], opcode[0], ~opcode[1], ~opcode[2], ~opcode[3], ~opcode[4]);  // AND_Gate
  and isCmp (ALUsignals[0], opcode[0], ~opcode[1], opcode[2], ~opcode[3], ~opcode[4]);  // AND_Gate
  and isMov (ALUsignals[6], opcode[0], ~opcode[1], opcode[3], ~opcode[4]);  // AND_Gate
  and and_7 (isRet, ~opcode[0], ~opcode[1], opcode[2], ~opcode[3], opcode[4]);  // AND_Gate
  and and_8 (isBeq, ~opcode[0], ~opcode[1], ~opcode[2], ~opcode[3], opcode[4]);  // AND_Gate
  and isMul (ALUsignals[3], ~opcode[0], opcode[1], ~opcode[2], ~opcode[3], ~opcode[4]);  // AND_Gate
  and and_9 (isSt, opcode[0], opcode[1], opcode[2], opcode[3], ~opcode[4]);  // AND_Gate
  and and_10 (and_10_out, opcode[1], ~opcode[2], ~opcode[3], opcode[4]);  // AND_Gate
  and and_11 (and_11_out, ~opcode[0], ~opcode[1], opcode[2], ~opcode[3], opcode[4]);  // AND_Gate
  and isLsr (ALUsignals[8], opcode[0], opcode[1], ~opcode[2], opcode[3], ~opcode[4]);  // AND_Gate
  or or_1 (isUbranch, and_10_out, and_11_out);
  and isLsl (ALUsignals[7], ~opcode[0], opcode[1], ~opcode[2], opcode[3], ~opcode[4]);  // AND_Gate
  and isMod (ALUsignals[5], ~opcode[0], ~opcode[1], opcode[2], ~opcode[3], ~opcode[4]);  // AND_Gate
  and isOr (ALUsignals[12], opcode[0], opcode[1], opcode[2], ~opcode[3], ~opcode[4]);  // AND_Gate
  and isDiv (ALUsignals[4], opcode[0], opcode[1], ~opcode[2], ~opcode[3], ~opcode[4]);  // AND_Gate
  and isAsr (ALUsignals[9], ~opcode[0], ~opcode[1], opcode[2], opcode[3], ~opcode[4]);  // AND_Gate
  and and_12 (isCall, opcode[0], opcode[1], ~opcode[2], ~opcode[3], opcode[4]);  // AND_Gate
  and and_13 (isLd, ~opcode[0], opcode[1], opcode[2], opcode[3], ~opcode[4]);  // AND_Gate

  assign isImmediate = I_bit;

  // Other names for the same wires on the sheet: O3 = ALUsignals[0]; O1 = ALUsignals[1]; O2 = ALUsignals[2];
  //   O4 = ALUsignals[3]; O5 = ALUsignals[4]; O6 = ALUsignals[5]; O13 = ALUsignals[6]; O7 = ALUsignals[7];
  //   O8 = ALUsignals[8]; O9 = ALUsignals[9]; O12 = ALUsignals[10]; O11 = ALUsignals[11]; O10 = ALUsignals[12];
  //   I = I_bit; a = opcode[0]; b = opcode[1]; c = opcode[2]; d = opcode[3]; e = opcode[4]

  // Notes on the sheet:
  //   op1
  //   op2
  //   op3
  //   op4
  //   op5
endmodule

module Program_Counter (
  input  Input___Enable,
  input  [31:0] Input_Data,
  input  Hit_Miss,
  input  Load_Store,
  input  Reset,
  input  isBranchTaken,
  input  [31:0] branchPC,
  input  Clock,
  output [31:0] Instruction
);

  wire and_1_out, not_1_out;
  wire [31:0] multiplexer_1_out, multiplexer_2_out, new_instruction;

  not not_1 (not_1_out, Hit_Miss);
  and and_1 (and_1_out, Load_Store, not_1_out);
  Multiplexer #(.width(32), .enable("false")) multiplexer_1 (
    .in0(multiplexer_2_out), .in1(Instruction), .out(multiplexer_1_out), .sel(and_1_out));
  Register #(.width(32)) register_1 (.D(multiplexer_1_out), .Q(Instruction), .clk(Clock), .clr(Reset));  // open: en
  Multiplexer #(.width(32)) multiplexer_2 (
    .in0(new_instruction), .in1(branchPC), .out(multiplexer_2_out), .sel(isBranchTaken));  // open: en
  Adder #(.width(32)) adder_1 (.a(32'h1), .b(Instruction), .out(new_instruction));  // open: cin, cout

  // Other names for the same wires on the sheet: in_data[31:0] = Input_Data; in_en = Input___Enable
endmodule

// FLAG
module Flags (
  input  in_1,
  input  isCmp,
  input  GREATER_THAN,
  input  EQUAL_TO,
  output flagsGT,
  output flagsE
);

  Register #(.width(1)) register_1 (.D(GREATER_THAN), .en(isCmp), .Q(flagsGT), .clk(in_1));  // open: clr
  Register #(.width(1)) register_2 (.D(EQUAL_TO), .en(isCmp), .Q(flagsE), .clk(in_1));  // open: clr

  // Other names for the same wires on the sheet: Clock = in_1
endmodule

// UNIT FOR BRANCHING CONDITION
module Branch (
  input  isBeq,
  input  flagsE,
  input  isUBranch,
  input  isBgt,
  input  flagsGT,
  output isBranchTaken
);

  wire Output1, Output2;

  and and_1 (Output1, isBeq, flagsE);
  and and_2 (Output2, isBgt, flagsGT);
  or or_1 (isBranchTaken, Output1, isUBranch, Output2);

  // Notes on the sheet:
  //   BRANCH IF EQUAL CONDITION
  //   BRANCH IF GREATER THAN CONDITION
endmodule

module Immediate_Calculation (
  input  [31:0] Operand_1,
  input  isRet,
  input  isImmediate,
  input  [31:0] Operand_2,
  input  [31:0] Instruction,
  input  [31:0] PC,
  output [31:0] Operand_2_prime,
  output [31:0] branchTarget
);

  wire [31:0] adder_1_out, bit_extender_1_out, bit_extender_2_out, bit_extender_3_out, bit_extender_4_out,
       Immx, shifter_1_out;

  assign bit_extender_1_out = {{16{1'b0}}, Instruction[15:0]};  // Bit_Extender bit_extender_1
  assign bit_extender_2_out = {{16{1'b0}}, Instruction[15:0]};  // Bit_Extender bit_extender_2
  assign bit_extender_3_out = {{5{1'b0}}, Instruction[26:0]};  // Bit_Extender bit_extender_3
  assign bit_extender_4_out = {{16{Instruction[15]}}, Instruction[15:0]};  // Bit_Extender bit_extender_4
  Shifter #(.width(32)) shifter_1 (.in(bit_extender_2_out), .\dist (5'b10000), .out(shifter_1_out));
  Adder #(.width(32)) adder_1 (.a(bit_extender_3_out), .b(PC), .out(adder_1_out));  // open: cin, cout
  Multiplexer #(.select(2), .width(32), .enable("false")) multiplexer_1 (
    .in0(bit_extender_4_out), .in1(bit_extender_1_out), .in2(shifter_1_out), .out(Immx),
    .sel(Instruction[17:16]));  // open: in3
  Multiplexer #(.width(32), .enable("false")) multiplexer_2 (
    .in0(adder_1_out), .in1(Operand_1), .out(branchTarget), .sel(isRet));
  Multiplexer #(.width(32), .enable("false")) multiplexer_3 (
    .in0(Operand_2), .in1(Immx), .out(Operand_2_prime), .sel(isImmediate));

  // Other names for the same wires on the sheet: Immediate = isImmediate; Return = isRet

  // Notes on the sheet:
  //   For selecting between immediate and register
endmodule
